# Fritzing sketch Alexa_GaesteWLAN_Switch (saved by Fritzing 0.9.3b)
breadboards: 2

parts:
  R1 = Resistor [tolerance=±5% resistance=470 package=THT]
  R2 = Trimmer Potentiometer [maximum_resistance=10kΩ package=THT]
  U1 = ESP32-38PinWide [part_number=ESP32-38PinWide]
  GLCD_128x1 = 128 x 64 Graphic LCD
  Q1 = NPN-Transistor [part_number=BC547 package="TO92 [THT]"]
  S1 = Pushbutton [package="[THT]"]

nets:
  N1: R1.Pin_0, Q1.B
  N2: R1.Pin_1, U1.GPIO4
  N3: R2.leg1, GLCD_128x1.3_Vo
  N4: R2.leg2, U1.VIN, GLCD_128x1.2_Vdd, GLCD_128x1.19_A(+)
  N5: U1.GND, GLCD_128x1.1_Vss, Q1.E, S1.Pin_3, S1.Pin_4
  N6: U1.GPIO17, S1.Pin_1, S1.Pin_2
  N7: U1.GPIO5, GLCD_128x1.4_D/I
  N8: U1.GPIO18, GLCD_128x1.6_Enable
  N9: U1.GPIO22, GLCD_128x1.17_RST
  N10: U1.GPIO23, GLCD_128x1.5_R/W
  N11: GLCD_128x1.20_K(-), Q1.C

custom parts:
  ESP32-38PinWide: Generic 38-Pin ESP32 with wide format (only access to one side of pins on a breadboard) based on Stephen Lilley's HiLetgo ESP-WROOM-32 ESP32 ESP-32S Development Board.
